# Fritzing sketch mbedagotchi (saved by Fritzing 0.9.10b)
breadboards: 1

parts:
  Nano = Arduino Nano (Rev3.0)
  LED1 = LED - 5mm [color="Red (633nm)" current=0.030 package="5 mm [THT]"]
  R1 = Resistor [tolerance=±5% power=0.25 resistance=220 package=THT]
  U1 = SPI_FLASH-X25XX [package=so08]

nets:
  N1: Nano.D2, R1.Pin_0
  N2: Nano.D11/MOSI, U1.MOSI
  N3: Nano.D12/MISO, U1.MISO
  GND: Nano.GND, LED1.cathode, U1.GND
  3V3: Nano.3V3, U1.VCC
  N4: LED1.anode, R1.Pin_1
